// Logisim project cdm-paint.circ as structural Verilog: 7 circuits, main circuit main
// rising
module main (
);

  wire and_1_out, and_2_out, and_4_out, and_5_out, and_6_out, and_7_out, and_8_out, and_9_out, button_1_out,
       button_2_out, button_3_out, button_4_out, cdm_16_1_p3, cdm_16_1_p5, cdm_16_1_p6, cdm_16_1_p7,
       cdm_16_1_p8, clk, comparator_1_eq, comparator_2_eq, comparator_3_eq, comparator_4_eq, comparator_5_eq,
       comparator_6_eq, comparator_7_eq, comparator_8_eq, comparator_9_eq, comparator_10_eq,
       comparator_11_eq, demultiplexer_1_out0, demultiplexer_1_out1, demultiplexer_1_out2,
       demultiplexer_1_out3, demultiplexer_1_out4, demultiplexer_1_out5, demultiplexer_1_out6,
       demultiplexer_1_out7, gamepad_1_irq, interrupt_arbiter_1_iack_1, interrupt_arbiter_1_iack_2,
       interrupt_arbiter_1_irq_out, menu_1_term_clock, menu_1_term_enable, not_1_out, priority_encoder_1_gs,
       ram_1_p3, timer_interrupt_1_irq, tInt;
  wire [1:0] joystick_1_x, joystick_1_y, uart_1_p6;
  wire [2:0] priority_encoder_1_out;
  wire [4:0] controlled_buffer_1_out, row_index_q;
  wire [5:0] interrupt_arbiter_1_vec_out, menu_1_cursor_col;
  wire [6:0] menu_1_term_data;
  wire [7:0] menu_cursor_pos_q, menu_data_q, uart_1_p1, uart_1_p2;
  wire [7:5] controlled_buffer_1_out_2;
  wire [15:0] cdm_16_1_p9, cdm_16_1_p10, cdm_16_1_p11, cursor_1_pos_q, cursor_2_pos_q, gamepad_1_data,
       row_high_q, row_low_q;
  wire [15:8] controlled_buffer_1_out_3;
  wire [31:0] cursor_1_o1, cursor_1_o2, cursor_1_o3, cursor_1_o4, cursor_1_o5, cursor_1_o6, cursor_1_o7,
       cursor_1_o8, cursor_1_o9, cursor_1_o10, cursor_1_o11, cursor_1_o12, cursor_1_o13, cursor_1_o14,
       cursor_1_o15, cursor_1_o16, cursor_1_o17, cursor_1_o18, cursor_1_o19, cursor_1_o20, cursor_1_o21,
       cursor_1_o22, cursor_1_o23, cursor_1_o24, cursor_1_o25, cursor_1_o26, cursor_1_o27, cursor_1_o28,
       cursor_1_o29, cursor_1_o30, cursor_1_o31, cursor_1_o32, cursor_2_o1, cursor_2_o2, cursor_2_o3,
       cursor_2_o4, cursor_2_o5, cursor_2_o6, cursor_2_o7, cursor_2_o8, cursor_2_o9, cursor_2_o10,
       cursor_2_o11, cursor_2_o12, cursor_2_o13, cursor_2_o14, cursor_2_o15, cursor_2_o16, cursor_2_o17,
       cursor_2_o18, cursor_2_o19, cursor_2_o20, cursor_2_o21, cursor_2_o22, cursor_2_o23, cursor_2_o24,
       cursor_2_o25, cursor_2_o26, cursor_2_o27, cursor_2_o28, cursor_2_o29, cursor_2_o30, cursor_2_o31,
       cursor_2_o32, display_adapter_1_o1, display_adapter_1_o2, display_adapter_1_o3, display_adapter_1_o4,
       display_adapter_1_o5, display_adapter_1_o6, display_adapter_1_o7, display_adapter_1_o8,
       display_adapter_1_o9, display_adapter_1_o10, display_adapter_1_o11, display_adapter_1_o12,
       display_adapter_1_o13, display_adapter_1_o14, display_adapter_1_o15, display_adapter_1_o16,
       display_adapter_1_o17, display_adapter_1_o18, display_adapter_1_o19, display_adapter_1_o20,
       display_adapter_1_o21, display_adapter_1_o22, display_adapter_1_o23, display_adapter_1_o24,
       display_adapter_1_o25, display_adapter_1_o26, display_adapter_1_o27, display_adapter_1_o28,
       display_adapter_1_o29, display_adapter_1_o30, display_adapter_1_o31, display_adapter_1_o32;

  timer_interrupt timer_interrupt_1 (
    .enable(tInt), .IRQ(timer_interrupt_1_irq), .IAck(interrupt_arbiter_1_iack_2), .clock(clk));
  interrupt_arbiter interrupt_arbiter_1 (
    .IRQ_2(timer_interrupt_1_irq), .vec_2(6'b010001), .IAck_2(interrupt_arbiter_1_iack_2),
    .IRQ_out(interrupt_arbiter_1_irq_out), .vec_out(interrupt_arbiter_1_vec_out), .IAck_out(cdm_16_1_p3),
    .IRQ_1(gamepad_1_irq), .vec_1(6'b010000), .IAck_1(interrupt_arbiter_1_iack_1), .clk(clk));
  Clock clock_1 (.out(clk));
  // CdM_16 cdm_16_1: pin names not known; wires that end beside it: interrupt_arbiter_1_irq_out, interrupt_arbiter_1_vec_out, cdm_16_1_p3, clk, cdm_16_1_p5, cdm_16_1_p6, cdm_16_1_p7, cdm_16_1_p8, cdm_16_1_p9, cdm_16_1_p10, cdm_16_1_p11
  Comparator #(.width(16), .mode("unsigned")) comparator_1 (
    .a({16{1'b0}}), .b(cdm_16_1_p9), .eq(comparator_1_eq));  // open: gt, lt
  Comparator #(.width(16), .mode("unsigned")) comparator_2 (
    .a(16'h2), .b(cdm_16_1_p9), .eq(comparator_2_eq));  // open: gt, lt
  Comparator #(.width(16), .mode("unsigned")) comparator_3 (
    .a(16'h4), .b(cdm_16_1_p9), .eq(comparator_3_eq));  // open: gt, lt
  Comparator #(.width(16), .mode("unsigned")) comparator_4 (
    .a(16'h5), .b(cdm_16_1_p9), .eq(comparator_4_eq));  // open: gt, lt
  Comparator #(.width(16), .mode("unsigned")) comparator_5 (
    .a(16'h6), .b(cdm_16_1_p9), .eq(comparator_5_eq));  // open: gt, lt
  Comparator #(.width(16), .mode("unsigned")) comparator_6 (
    .a(16'h8), .b(cdm_16_1_p9), .eq(comparator_6_eq));  // open: gt, lt
  Comparator #(.width(16), .mode("unsigned")) comparator_7 (
    .a(16'ha), .b(cdm_16_1_p9), .eq(comparator_7_eq));  // open: gt, lt
  Comparator #(.width(16), .mode("unsigned")) comparator_8 (
    .a(16'hb), .b(cdm_16_1_p9), .eq(comparator_8_eq));  // open: gt, lt
  Comparator #(.width(16), .mode("unsigned")) comparator_9 (
    .a(16'hc), .b(cdm_16_1_p9), .eq(comparator_9_eq));  // open: gt, lt
  Comparator #(.width(16), .mode("unsigned")) comparator_10 (
    .a(16'hd), .b(cdm_16_1_p9), .eq(comparator_10_eq));  // open: gt, lt
  Comparator #(.width(16), .mode("unsigned")) comparator_11 (
    .a(16'he), .b(cdm_16_1_p9), .eq(comparator_11_eq));  // open: gt, lt
  and and_1 (and_1_out, cdm_16_1_p5, cdm_16_1_p6);
  and and_2 (and_2_out, ~cdm_16_1_p5, cdm_16_1_p6);  // AND_Gate
  Priority_Encoder priority_encoder_1 (
    .in0(comparator_1_eq), .in1(comparator_2_eq), .in2(comparator_3_eq), .in3(comparator_4_eq),
    .in4(comparator_5_eq), .in5(comparator_6_eq), .in6(comparator_7_eq), .in7(comparator_8_eq),
    .out(priority_encoder_1_out), .gs(priority_encoder_1_gs));  // open: en_in, en_out
  not not_1 (not_1_out, cdm_16_1_p7);
  assign {controlled_buffer_1_out_3, controlled_buffer_1_out_2, controlled_buffer_1_out} = not_1_out ? cdm_16_1_p10 : 16'bz;  // Controlled_Buffer controlled_buffer_1
  assign cdm_16_1_p11 = cdm_16_1_p7 ? {controlled_buffer_1_out_3, controlled_buffer_1_out_2, controlled_buffer_1_out} : 16'bz;  // Controlled_Buffer controlled_buffer_2
  // RAM ram_1: pin names not known; wires that end beside it: cdm_16_1_p9, cdm_16_1_p8, ram_1_p3, clk, cdm_16_1_p7, {controlled_buffer_1_out_3, controlled_buffer_1_out_2, controlled_buffer_1_out}
  // ROM rom_1: pin names not known; wires that end beside it: cdm_16_1_p9, and_2_out, cdm_16_1_p8, {controlled_buffer_1_out_3, controlled_buffer_1_out_2, controlled_buffer_1_out}
  and and_3 (ram_1_p3, ~and_7_out, ~and_6_out, ~and_5_out, and_1_out);  // AND_Gate
  and and_4 (and_4_out, priority_encoder_1_gs, and_1_out, ~cdm_16_1_p7);  // AND_Gate
  Demultiplexer #(.select(3), .disabled(0)) demultiplexer_1 (
    .out0(demultiplexer_1_out0), .out1(demultiplexer_1_out1), .out2(demultiplexer_1_out2),
    .out3(demultiplexer_1_out3), .out4(demultiplexer_1_out4), .out5(demultiplexer_1_out5),
    .out6(demultiplexer_1_out6), .out7(demultiplexer_1_out7), .in(1'b1), .sel(priority_encoder_1_out),
    .en(and_4_out));
  and and_5 (and_5_out, comparator_9_eq, and_1_out, cdm_16_1_p7);
  and and_6 (and_6_out, comparator_10_eq, and_1_out, cdm_16_1_p7);
  and and_7 (and_7_out, comparator_11_eq, and_1_out);
  and and_8 (and_8_out, and_7_out, cdm_16_1_p7);
  and and_9 (and_9_out, and_7_out, ~cdm_16_1_p7);  // AND_Gate
  // UART uart_1: pin names not known; wires that end beside it: uart_1_p1, uart_1_p2, uart_1_p6[1], clk, cdm_16_1_p7, uart_1_p6[0], and_7_out
  assign {controlled_buffer_1_out_2, controlled_buffer_1_out} = and_8_out ? uart_1_p1 : 8'bz;  // Controlled_Buffer controlled_buffer_3
  assign uart_1_p2 = and_9_out ? {controlled_buffer_1_out_2, controlled_buffer_1_out} : 8'bz;  // Controlled_Buffer controlled_buffer_4
  assign {controlled_buffer_1_out_3, controlled_buffer_1_out_2, controlled_buffer_1_out} = and_6_out ? {{14{1'b0}}, uart_1_p6} : 16'bz;  // Controlled_Buffer controlled_buffer_5
  Register #(.width(16)) row_low (
    .D({controlled_buffer_1_out_3, controlled_buffer_1_out_2, controlled_buffer_1_out}),
    .en(demultiplexer_1_out0), .Q(row_low_q), .clk(clk));  // open: clr
  Register #(.width(16)) row_high (
    .D({controlled_buffer_1_out_3, controlled_buffer_1_out_2, controlled_buffer_1_out}),
    .en(demultiplexer_1_out1), .Q(row_high_q), .clk(clk));  // open: clr
  Register #(.width(5)) row_index (
    .D(controlled_buffer_1_out), .en(demultiplexer_1_out2), .Q(row_index_q), .clk(clk));  // open: clr
  Register #(.width(1)) timer_int_enable (
    .D(controlled_buffer_1_out[0]), .en(demultiplexer_1_out3), .Q(tInt), .clk(clk));  // open: clr
  Register #(.width(16)) cursor_1_pos (
    .D({controlled_buffer_1_out_3, controlled_buffer_1_out_2, controlled_buffer_1_out}),
    .en(demultiplexer_1_out4), .Q(cursor_1_pos_q), .clk(clk));  // open: clr
  Register #(.width(16)) cursor_2_pos (
    .D({controlled_buffer_1_out_3, controlled_buffer_1_out_2, controlled_buffer_1_out}),
    .en(demultiplexer_1_out5), .Q(cursor_2_pos_q), .clk(clk));  // open: clr
  Register menu_data (
    .D({controlled_buffer_1_out_2, controlled_buffer_1_out}), .en(demultiplexer_1_out6), .Q(menu_data_q),
    .clk(clk));  // open: clr
  Register menu_cursor_pos (
    .D({controlled_buffer_1_out_2, controlled_buffer_1_out}), .en(demultiplexer_1_out7),
    .Q(menu_cursor_pos_q), .clk(clk));  // open: clr
  assign {controlled_buffer_1_out_3, controlled_buffer_1_out_2, controlled_buffer_1_out} = and_5_out ? gamepad_1_data : 16'bz;  // Controlled_Buffer controlled_buffer_6
  display_adapter display_adapter_1 (
    .data({row_low_q, row_high_q}), .o1(display_adapter_1_o1), .o2(display_adapter_1_o2),
    .o3(display_adapter_1_o3), .o4(display_adapter_1_o4), .o5(display_adapter_1_o5),
    .o6(display_adapter_1_o6), .o7(display_adapter_1_o7), .o8(display_adapter_1_o8),
    .o9(display_adapter_1_o9), .o10(display_adapter_1_o10), .o11(display_adapter_1_o11),
    .o12(display_adapter_1_o12), .o13(display_adapter_1_o13), .o14(display_adapter_1_o14),
    .o15(display_adapter_1_o15), .o16(display_adapter_1_o16), .o17(display_adapter_1_o17),
    .o18(display_adapter_1_o18), .o19(display_adapter_1_o19), .o20(display_adapter_1_o20),
    .o21(display_adapter_1_o21), .o22(display_adapter_1_o22), .o23(display_adapter_1_o23),
    .o24(display_adapter_1_o24), .o25(display_adapter_1_o25), .o26(display_adapter_1_o26),
    .o27(display_adapter_1_o27), .o28(display_adapter_1_o28), .o29(display_adapter_1_o29),
    .o30(display_adapter_1_o30), .o31(display_adapter_1_o31), .o32(display_adapter_1_o32),
    .index(row_index_q), .enable(demultiplexer_1_out1), .clock(clk));
  cursor cursor_1 (
    .cursor(cursor_1_pos_q), .i1(display_adapter_1_o1), .i2(display_adapter_1_o2), .i3(display_adapter_1_o3),
    .i4(display_adapter_1_o4), .i5(display_adapter_1_o5), .i6(display_adapter_1_o6),
    .i7(display_adapter_1_o7), .i8(display_adapter_1_o8), .i9(display_adapter_1_o9),
    .i10(display_adapter_1_o10), .i11(display_adapter_1_o11), .i12(display_adapter_1_o12),
    .i13(display_adapter_1_o13), .i14(display_adapter_1_o14), .i15(display_adapter_1_o15),
    .i16(display_adapter_1_o16), .i17(display_adapter_1_o17), .i18(display_adapter_1_o18),
    .i19(display_adapter_1_o19), .i20(display_adapter_1_o20), .i21(display_adapter_1_o21),
    .i22(display_adapter_1_o22), .i23(display_adapter_1_o23), .i24(display_adapter_1_o24),
    .i25(display_adapter_1_o25), .i26(display_adapter_1_o26), .i27(display_adapter_1_o27),
    .i28(display_adapter_1_o28), .i29(display_adapter_1_o29), .i30(display_adapter_1_o30),
    .i31(display_adapter_1_o31), .i32(display_adapter_1_o32), .o1(cursor_1_o1), .o2(cursor_1_o2),
    .o3(cursor_1_o3), .o4(cursor_1_o4), .o5(cursor_1_o5), .o6(cursor_1_o6), .o7(cursor_1_o7),
    .o8(cursor_1_o8), .o9(cursor_1_o9), .o10(cursor_1_o10), .o11(cursor_1_o11), .o12(cursor_1_o12),
    .o13(cursor_1_o13), .o14(cursor_1_o14), .o15(cursor_1_o15), .o16(cursor_1_o16), .o17(cursor_1_o17),
    .o18(cursor_1_o18), .o19(cursor_1_o19), .o20(cursor_1_o20), .o21(cursor_1_o21), .o22(cursor_1_o22),
    .o23(cursor_1_o23), .o24(cursor_1_o24), .o25(cursor_1_o25), .o26(cursor_1_o26), .o27(cursor_1_o27),
    .o28(cursor_1_o28), .o29(cursor_1_o29), .o30(cursor_1_o30), .o31(cursor_1_o31), .o32(cursor_1_o32),
    .clock(clk));
  DotMatrix #(.inputtype("row"), .matrixcols(32), .matrixrows(32)) dotmatrix_1 (
    .row0(cursor_2_o1), .row1(cursor_2_o2), .row2(cursor_2_o3), .row3(cursor_2_o4), .row4(cursor_2_o5),
    .row5(cursor_2_o6), .row6(cursor_2_o7), .row7(cursor_2_o8), .row8(cursor_2_o9), .row9(cursor_2_o10),
    .row10(cursor_2_o11), .row11(cursor_2_o12), .row12(cursor_2_o13), .row13(cursor_2_o14),
    .row14(cursor_2_o15), .row15(cursor_2_o16), .row16(cursor_2_o17), .row17(cursor_2_o18),
    .row18(cursor_2_o19), .row19(cursor_2_o20), .row20(cursor_2_o21), .row21(cursor_2_o22),
    .row22(cursor_2_o23), .row23(cursor_2_o24), .row24(cursor_2_o25), .row25(cursor_2_o26),
    .row26(cursor_2_o27), .row27(cursor_2_o28), .row28(cursor_2_o29), .row29(cursor_2_o30),
    .row30(cursor_2_o31), .row31(cursor_2_o32));
  cursor cursor_2 (
    .cursor(cursor_2_pos_q), .i1(cursor_1_o1), .i2(cursor_1_o2), .i3(cursor_1_o3), .i4(cursor_1_o4),
    .i5(cursor_1_o5), .i6(cursor_1_o6), .i7(cursor_1_o7), .i8(cursor_1_o8), .i9(cursor_1_o9),
    .i10(cursor_1_o10), .i11(cursor_1_o11), .i12(cursor_1_o12), .i13(cursor_1_o13), .i14(cursor_1_o14),
    .i15(cursor_1_o15), .i16(cursor_1_o16), .i17(cursor_1_o17), .i18(cursor_1_o18), .i19(cursor_1_o19),
    .i20(cursor_1_o20), .i21(cursor_1_o21), .i22(cursor_1_o22), .i23(cursor_1_o23), .i24(cursor_1_o24),
    .i25(cursor_1_o25), .i26(cursor_1_o26), .i27(cursor_1_o27), .i28(cursor_1_o28), .i29(cursor_1_o29),
    .i30(cursor_1_o30), .i31(cursor_1_o31), .i32(cursor_1_o32), .o1(cursor_2_o1), .o2(cursor_2_o2),
    .o3(cursor_2_o3), .o4(cursor_2_o4), .o5(cursor_2_o5), .o6(cursor_2_o6), .o7(cursor_2_o7),
    .o8(cursor_2_o8), .o9(cursor_2_o9), .o10(cursor_2_o10), .o11(cursor_2_o11), .o12(cursor_2_o12),
    .o13(cursor_2_o13), .o14(cursor_2_o14), .o15(cursor_2_o15), .o16(cursor_2_o16), .o17(cursor_2_o17),
    .o18(cursor_2_o18), .o19(cursor_2_o19), .o20(cursor_2_o20), .o21(cursor_2_o21), .o22(cursor_2_o22),
    .o23(cursor_2_o23), .o24(cursor_2_o24), .o25(cursor_2_o25), .o26(cursor_2_o26), .o27(cursor_2_o27),
    .o28(cursor_2_o28), .o29(cursor_2_o29), .o30(cursor_2_o30), .o31(cursor_2_o31), .o32(cursor_2_o32),
    .clock(clk));
  Button button_1 (.out(button_1_out));
  Joystick #(.bits(2)) joystick_1 (.x(joystick_1_x), .y(joystick_1_y));
  gamepad gamepad_1 (
    .data(gamepad_1_data), .joy({joystick_1_y, joystick_1_x}), .B(button_4_out), .A(button_3_out),
    .R(button_2_out), .IAck(interrupt_arbiter_1_iack_1), .clk(clk), .IRQ(gamepad_1_irq), .L(button_1_out));
  Button button_2 (.out(button_2_out));
  Button button_3 (.out(button_3_out));
  Button button_4 (.out(button_4_out));
  TTY #(.rows(3), .cols(16), .trigger("falling")) tty_1 (
    .data(menu_1_term_data), .clk(menu_1_term_clock), .we(menu_1_term_enable));  // open: clr
  DotMatrix #(.matrixcols(1), .matrixrows(6)) dotmatrix_2 (.col0(menu_1_cursor_col));
  menu menu_1 (
    .cursor_col(menu_1_cursor_col), .term_data(menu_1_term_data), .term_clock(menu_1_term_clock),
    .term_enable(menu_1_term_enable), .cursor(menu_cursor_pos_q), .data(menu_data_q), .clock(clk));

  // Notes on the sheet:
  //   screen row low
  //   screen row high
  //   screen row index
  //   timer interrupt enable
  //   screen cursor 1 position
  //   screen cursor 2 position
  //   menu data
  //   menu cursor position
  //   gamepad data
  //   uart flags
  //   uart data
endmodule

module interrupt_arbiter (
  input  IRQ_2,
  input  [5:0] vec_2,
  input  IAck_out,
  input  IRQ_1,
  input  [5:0] vec_1,
  input  clk,
  output IRQ_out,
  output [5:0] vec_out,
  output IAck_2,
  output IAck_1
);

  wire and_2_out, and_3_out, and_4_out, and_5_out, and_7_out, and_8_out, d_ff_1_q, d_ff_2_q, or_1_out,
       or_2_out;

  and and_1 (IAck_2, d_ff_1_q, IAck_out);
  and and_2 (and_2_out, IRQ_2, ~IRQ_1, ~d_ff_2_q);  // AND_Gate
  and and_3 (and_3_out, d_ff_1_q, IAck_out);
  and and_4 (and_4_out, ~d_ff_1_q, IRQ_1);  // AND_Gate
  and and_5 (and_5_out, d_ff_2_q, IAck_out);
  and and_6 (IAck_1, IAck_out, d_ff_2_q);
  or or_1 (or_1_out, and_2_out, and_3_out);
  or or_2 (or_2_out, and_4_out, and_5_out);
  D_Flip_Flop d_ff_1 (.clk(clk), .D(or_1_out), .Q(d_ff_1_q));  // open: Qn, preset, en, reset
  D_Flip_Flop d_ff_2 (.clk(clk), .D(or_2_out), .Q(d_ff_2_q));  // open: Qn, preset, en, reset
  and and_7 (and_7_out, d_ff_1_q, IAck_out);
  assign vec_out = and_7_out ? vec_2 : 6'bz;  // Controlled_Buffer controlled_buffer_1
  and and_8 (and_8_out, d_ff_2_q, IAck_out);
  assign vec_out = and_8_out ? vec_1 : 6'bz;  // Controlled_Buffer controlled_buffer_2
  assign IRQ_out = d_ff_1_q ? IRQ_2 : 1'bz;  // Controlled_Buffer controlled_buffer_3
  Pull_Resistor pull_resistor_1 (.node(IRQ_out));
  assign IRQ_out = d_ff_2_q ? IRQ_1 : 1'bz;  // Controlled_Buffer controlled_buffer_4
endmodule

module gamepad (
  input  IAck,
  input  clk,
  input  [3:0] joy,
  input  R,
  input  L,
  input  B,
  input  A,
  output [15:0] data,
  output IRQ
);

  wire and_5_out, comparator_1_eq;
  wire [5:2] and_3_out;
  wire [15:0] register_1_q;

  and and_1 (and_3_out[4], joy[0], joy[1]);
  and and_2 (and_3_out[5], joy[0], ~joy[1]);  // AND_Gate
  and and_3 (and_3_out[2], joy[2], joy[3]);
  and and_4 (and_3_out[3], joy[2], ~joy[3]);  // AND_Gate
  Register #(.width(16)) register_1 (
    .D({{8{1'b0}}, L, R, and_3_out, B, A}), .en(and_5_out), .Q(register_1_q), .clk(clk));  // open: clr
  and and_5 (and_5_out, ~IAck, comparator_1_eq);  // AND_Gate
  Register #(.width(16), .trigger("falling")) register_2 (
    .D(register_1_q), .en(IAck), .Q(data), .clk(clk));  // open: clr
  Comparator #(.width(16), .mode("unsigned")) comparator_1 (
    .a(data), .b(register_1_q), .eq(comparator_1_eq));  // open: gt, lt
  not not_1 (IRQ, comparator_1_eq);
endmodule

module display_adapter (
  input  clock,
  input  [31:0] data,
  input  [4:0] index,
  input  enable,
  output [31:0] o1,
  output [31:0] o2,
  output [31:0] o3,
  output [31:0] o4,
  output [31:0] o5,
  output [31:0] o6,
  output [31:0] o7,
  output [31:0] o8,
  output [31:0] o9,
  output [31:0] o10,
  output [31:0] o11,
  output [31:0] o12,
  output [31:0] o13,
  output [31:0] o14,
  output [31:0] o15,
  output [31:0] o16,
  output [31:0] o17,
  output [31:0] o18,
  output [31:0] o19,
  output [31:0] o20,
  output [31:0] o21,
  output [31:0] o22,
  output [31:0] o23,
  output [31:0] o24,
  output [31:0] o25,
  output [31:0] o26,
  output [31:0] o27,
  output [31:0] o28,
  output [31:0] o29,
  output [31:0] o30,
  output [31:0] o31,
  output [31:0] o32
);

  wire demultiplexer_1_out0, demultiplexer_1_out1, demultiplexer_1_out2, demultiplexer_1_out3,
       demultiplexer_1_out4, demultiplexer_1_out5, demultiplexer_1_out6, demultiplexer_1_out7,
       demultiplexer_1_out8, demultiplexer_1_out9, demultiplexer_1_out10, demultiplexer_1_out11,
       demultiplexer_1_out12, demultiplexer_1_out13, demultiplexer_1_out14, demultiplexer_1_out15,
       demultiplexer_1_out16, demultiplexer_1_out17, demultiplexer_1_out18, demultiplexer_1_out19,
       demultiplexer_1_out20, demultiplexer_1_out21, demultiplexer_1_out22, demultiplexer_1_out23,
       demultiplexer_1_out24, demultiplexer_1_out25, demultiplexer_1_out26, demultiplexer_1_out27,
       demultiplexer_1_out28, demultiplexer_1_out29, demultiplexer_1_out30, demultiplexer_1_out31;

  Demultiplexer #(.select(5), .disabled(0), .enable("false")) demultiplexer_1 (
    .out0(demultiplexer_1_out0), .out1(demultiplexer_1_out1), .out2(demultiplexer_1_out2),
    .out3(demultiplexer_1_out3), .out4(demultiplexer_1_out4), .out5(demultiplexer_1_out5),
    .out6(demultiplexer_1_out6), .out7(demultiplexer_1_out7), .out8(demultiplexer_1_out8),
    .out9(demultiplexer_1_out9), .out10(demultiplexer_1_out10), .out11(demultiplexer_1_out11),
    .out12(demultiplexer_1_out12), .out13(demultiplexer_1_out13), .out14(demultiplexer_1_out14),
    .out15(demultiplexer_1_out15), .out16(demultiplexer_1_out16), .out17(demultiplexer_1_out17),
    .out18(demultiplexer_1_out18), .out19(demultiplexer_1_out19), .out20(demultiplexer_1_out20),
    .out21(demultiplexer_1_out21), .out22(demultiplexer_1_out22), .out23(demultiplexer_1_out23),
    .out24(demultiplexer_1_out24), .out25(demultiplexer_1_out25), .out26(demultiplexer_1_out26),
    .out27(demultiplexer_1_out27), .out28(demultiplexer_1_out28), .out29(demultiplexer_1_out29),
    .out30(demultiplexer_1_out30), .out31(demultiplexer_1_out31), .in(enable), .sel(index));
  Register #(.width(32), .trigger("falling")) register_1 (
    .D(data), .en(demultiplexer_1_out0), .Q(o1), .clk(clock));  // open: clr
  Register #(.width(32), .trigger("falling")) register_2 (
    .D(data), .en(demultiplexer_1_out1), .Q(o2), .clk(clock));  // open: clr
  Register #(.width(32), .trigger("falling")) register_3 (
    .D(data), .en(demultiplexer_1_out2), .Q(o3), .clk(clock));  // open: clr
  Register #(.width(32), .trigger("falling")) register_4 (
    .D(data), .en(demultiplexer_1_out3), .Q(o4), .clk(clock));  // open: clr
  Register #(.width(32), .trigger("falling")) register_5 (
    .D(data), .en(demultiplexer_1_out4), .Q(o5), .clk(clock));  // open: clr
  Register #(.width(32), .trigger("falling")) register_6 (
    .D(data), .en(demultiplexer_1_out5), .Q(o6), .clk(clock));  // open: clr
  Register #(.width(32), .trigger("falling")) register_7 (
    .D(data), .en(demultiplexer_1_out6), .Q(o7), .clk(clock));  // open: clr
  Register #(.width(32), .trigger("falling")) register_8 (
    .D(data), .en(demultiplexer_1_out7), .Q(o8), .clk(clock));  // open: clr
  Register #(.width(32), .trigger("falling")) register_9 (
    .D(data), .en(demultiplexer_1_out8), .Q(o9), .clk(clock));  // open: clr
  Register #(.width(32), .trigger("falling")) register_10 (
    .D(data), .en(demultiplexer_1_out9), .Q(o10), .clk(clock));  // open: clr
  Register #(.width(32), .trigger("falling")) register_11 (
    .D(data), .en(demultiplexer_1_out10), .Q(o11), .clk(clock));  // open: clr
  Register #(.width(32), .trigger("falling")) register_12 (
    .D(data), .en(demultiplexer_1_out11), .Q(o12), .clk(clock));  // open: clr
  Register #(.width(32), .trigger("falling")) register_13 (
    .D(data), .en(demultiplexer_1_out12), .Q(o13), .clk(clock));  // open: clr
  Register #(.width(32), .trigger("falling")) register_14 (
    .D(data), .en(demultiplexer_1_out13), .Q(o14), .clk(clock));  // open: clr
  Register #(.width(32), .trigger("falling")) register_15 (
    .D(data), .en(demultiplexer_1_out14), .Q(o15), .clk(clock));  // open: clr
  Register #(.width(32), .trigger("falling")) register_16 (
    .D(data), .en(demultiplexer_1_out15), .Q(o16), .clk(clock));  // open: clr
  Register #(.width(32), .trigger("falling")) register_17 (
    .D(data), .en(demultiplexer_1_out16), .Q(o17), .clk(clock));  // open: clr
  Register #(.width(32), .trigger("falling")) register_18 (
    .D(data), .en(demultiplexer_1_out17), .Q(o18), .clk(clock));  // open: clr
  Register #(.width(32), .trigger("falling")) register_19 (
    .D(data), .en(demultiplexer_1_out18), .Q(o19), .clk(clock));  // open: clr
  Register #(.width(32), .trigger("falling")) register_20 (
    .D(data), .en(demultiplexer_1_out19), .Q(o20), .clk(clock));  // open: clr
  Register #(.width(32), .trigger("falling")) register_21 (
    .D(data), .en(demultiplexer_1_out20), .Q(o21), .clk(clock));  // open: clr
  Register #(.width(32), .trigger("falling")) register_22 (
    .D(data), .en(demultiplexer_1_out21), .Q(o22), .clk(clock));  // open: clr
  Register #(.width(32), .trigger("falling")) register_23 (
    .D(data), .en(demultiplexer_1_out22), .Q(o23), .clk(clock));  // open: clr
  Register #(.width(32), .trigger("falling")) register_24 (
    .D(data), .en(demultiplexer_1_out23), .Q(o24), .clk(clock));  // open: clr
  Register #(.width(32), .trigger("falling")) register_25 (
    .D(data), .en(demultiplexer_1_out24), .Q(o25), .clk(clock));  // open: clr
  Register #(.width(32), .trigger("falling")) register_26 (
    .D(data), .en(demultiplexer_1_out25), .Q(o26), .clk(clock));  // open: clr
  Register #(.width(32), .trigger("falling")) register_27 (
    .D(data), .en(demultiplexer_1_out26), .Q(o27), .clk(clock));  // open: clr
  Register #(.width(32), .trigger("falling")) register_28 (
    .D(data), .en(demultiplexer_1_out27), .Q(o28), .clk(clock));  // open: clr
  Register #(.width(32), .trigger("falling")) register_29 (
    .D(data), .en(demultiplexer_1_out28), .Q(o29), .clk(clock));  // open: clr
  Register #(.width(32), .trigger("falling")) register_30 (
    .D(data), .en(demultiplexer_1_out29), .Q(o30), .clk(clock));  // open: clr
  Register #(.width(32), .trigger("falling")) register_31 (
    .D(data), .en(demultiplexer_1_out30), .Q(o31), .clk(clock));  // open: clr
  Register #(.width(32), .trigger("falling")) register_32 (
    .D(data), .en(demultiplexer_1_out31), .Q(o32), .clk(clock));  // open: clr

  // Other names for the same wires on the sheet: clk = clock
endmodule

module menu (
  input  [7:0] cursor,
  input  [7:0] data,
  input  clock,
  output [5:0] cursor_col,
  output term_enable,
  output term_clock,
  output [6:0] term_data
);

  wire Char_counter_carry, comparator_1_eq, comparator_2_eq, nor_2_out, not_1_out, s_r_ff_1_qn,
       stable_clock_1_p1, stable_clock_1_p3;
  wire [5:0] Char_counter_q;
  wire [7:0] adder_1_out, multiplexer_1_out, multiplexer_2_out, multiplexer_3_out, multiplexer_4_out,
       register_1_q, register_2_q, register_3_q, register_4_q;

  Register register_1 (.D(cursor), .Q(register_1_q), .clk(clock));  // open: en, clr
  Register #(.trigger("falling")) register_2 (.D(cursor), .Q(register_2_q), .clk(clock));  // open: en, clr
  Comparator comparator_1 (.a(register_1_q), .b(register_2_q), .eq(comparator_1_eq));  // open: gt, lt
  Multiplexer #(.select(3), .width(8), .disabled(0), .enable("false")) multiplexer_1 (
    .in0(8'h20), .in1(8'h28), .in2(8'h30), .in3(8'h38), .in4(8'h40), .in5(8'h48), .in6({8{1'b0}}),
    .in7({8{1'b0}}), .out(multiplexer_1_out), .sel(register_3_q[2:0]));
  Multiplexer #(.width(8), .disabled(0), .enable("false")) multiplexer_2 (
    .in0(8'h50), .in1(8'h58), .out(multiplexer_2_out), .sel(register_3_q[3]));
  Counter #(.width(6), .max('h2f), .trigger("falling")) Char_counter (
    .count(term_enable), .Q(Char_counter_q), .carry(Char_counter_carry), .clk(clock));  // open: load, D, clr
  Register register_3 (.D(data), .en(not_1_out), .Q(register_3_q), .clk(clock));  // open: clr
  // stable_clock stable_clock_1: pin names not known; wires that end beside it: stable_clock_1_p1, clock, stable_clock_1_p3
  nor nor_1 (stable_clock_1_p1, cursor[7], ~comparator_1_eq);  // NOR_Gate
  Multiplexer #(.width(8), .disabled(0), .enable("false")) multiplexer_3 (
    .in0(8'h60), .in1(8'h68), .out(multiplexer_3_out), .sel(register_3_q[4]));
  Register #(.trigger("falling")) register_4 (
    .D(register_3_q), .en(Char_counter_carry), .Q(register_4_q), .clk(clock));  // open: clr
  nor nor_2 (nor_2_out, cursor[7], stable_clock_1_p3);
  Demultiplexer #(.select(2), .disabled(0), .enable("false")) demultiplexer_1 (
    .out0(cursor_col[4]), .out1(cursor_col[2]), .out2(cursor_col[0]), .in(nor_2_out), .sel(cursor[1:0]));  // open: out3
  Multiplexer #(.select(3), .width(8), .disabled(0), .enable("false")) multiplexer_4 (
    .in0(8'h8), .in1(multiplexer_1_out), .in2(8'h10), .in3(multiplexer_2_out), .in4(8'h18),
    .in5(multiplexer_3_out), .in6({8{1'b0}}), .in7({8{1'b0}}), .out(multiplexer_4_out),
    .sel(Char_counter_q[5:3]));
  Comparator comparator_2 (.a(register_3_q), .b(register_4_q), .eq(comparator_2_eq));  // open: gt, lt
  Adder adder_1 (.a(multiplexer_4_out), .b({{5{1'b0}}, Char_counter_q[2:0]}), .out(adder_1_out));  // open: cin, cout
  S_R_Flip_Flop #(.trigger("falling")) s_r_ff_1 (
    .S(Char_counter_carry), .clk(clock), .R(1'b0), .Qn(s_r_ff_1_qn));  // open: Q, preset, reset, en
  ROM #(.dataWidth(7)) rom_1 (.addr(adder_1_out), .data(term_data));  // open: sel
  or or_1 (term_enable, s_r_ff_1_qn, ~comparator_2_eq);  // OR_Gate
  not not_1 (not_1_out, term_enable);

  assign {cursor_col[5], cursor_col[3], cursor_col[1]} = 3'b000;
  assign term_clock = clock;

  // Notes on the sheet:
  //   Detects changes in
  //   cursor position
  //   These select the offsets of the
  //   8-byte blocks stored in ROM
  //   negative position
  //   = cursor is hidden
  //   Detects changes in data
  //   Locks the current value
  //   until the screen is refreshed
  //   Forms the column with the
  //   blinking cursor
  //   Character block ROM
  //   Refreshes the screen
  //   once after a reset
  //   contents of rom_1 (hex, n*v repeats v):
  //   55 6e 6b 6e 6f 77 6e 20 54 6f 6f 6c 3a 20 20 20 43 6f 6c 6f 72 3a 20 20 46 69 6c 6c 3a 20 20 20 50
  //   69 78 65 6c 20 20 20 4c 69 6e 65 4*20 52 65 63 74 4*20 45 6c 6c 69 70 73 65 20 42 75 63 6b 65 74 20
  //   20 43 6c 65 61 72 20 20 20 42 6c 61 63 6b 20 20 20 47 72 65 65 6e 20 20 20 4f 66 66 5*20 4f 6e 6*20
endmodule

module timer_interrupt (
  input  enable,
  input  clock,
  input  IAck,
  output IRQ
);

  wire and_1_out, d_ff_1_qn, stable_clock_1_p3;

  // stable_clock stable_clock_1: pin names not known; wires that end beside it: enable, clock, stable_clock_1_p3
  D_Flip_Flop #(.trigger("falling")) d_ff_1 (
    .clk(clock), .D(stable_clock_1_p3), .Qn(d_ff_1_qn));  // open: Q, preset, en, reset
  and and_1 (and_1_out, stable_clock_1_p3, d_ff_1_qn);
  S_R_Flip_Flop #(.trigger("falling")) s_r_ff_1 (
    .S(and_1_out), .clk(clock), .R(IAck), .Q(IRQ));  // open: Qn, preset, reset, en
endmodule

module cursor (
  input  [15:0] cursor,
  input  clock,
  input  [31:0] i1,
  input  [31:0] i2,
  input  [31:0] i3,
  input  [31:0] i4,
  input  [31:0] i5,
  input  [31:0] i6,
  input  [31:0] i7,
  input  [31:0] i8,
  input  [31:0] i9,
  input  [31:0] i10,
  input  [31:0] i11,
  input  [31:0] i12,
  input  [31:0] i13,
  input  [31:0] i14,
  input  [31:0] i15,
  input  [31:0] i16,
  input  [31:0] i17,
  input  [31:0] i18,
  input  [31:0] i19,
  input  [31:0] i20,
  input  [31:0] i21,
  input  [31:0] i22,
  input  [31:0] i23,
  input  [31:0] i24,
  input  [31:0] i25,
  input  [31:0] i26,
  input  [31:0] i27,
  input  [31:0] i28,
  input  [31:0] i29,
  input  [31:0] i30,
  input  [31:0] i31,
  input  [31:0] i32,
  output [31:0] o1,
  output [31:0] o2,
  output [31:0] o3,
  output [31:0] o4,
  output [31:0] o5,
  output [31:0] o6,
  output [31:0] o7,
  output [31:0] o8,
  output [31:0] o9,
  output [31:0] o10,
  output [31:0] o11,
  output [31:0] o12,
  output [31:0] o13,
  output [31:0] o14,
  output [31:0] o15,
  output [31:0] o16,
  output [31:0] o17,
  output [31:0] o18,
  output [31:0] o19,
  output [31:0] o20,
  output [31:0] o21,
  output [31:0] o22,
  output [31:0] o23,
  output [31:0] o24,
  output [31:0] o25,
  output [31:0] o26,
  output [31:0] o27,
  output [31:0] o28,
  output [31:0] o29,
  output [31:0] o30,
  output [31:0] o31,
  output [31:0] o32
);

  wire and_1_out, demultiplexer_1_out0, demultiplexer_1_out1, demultiplexer_1_out2, demultiplexer_1_out3,
       demultiplexer_1_out4, demultiplexer_1_out5, demultiplexer_1_out6, demultiplexer_1_out7,
       demultiplexer_1_out8, demultiplexer_1_out9, demultiplexer_1_out10, demultiplexer_1_out11,
       demultiplexer_1_out12, demultiplexer_1_out13, demultiplexer_1_out14, demultiplexer_1_out15,
       demultiplexer_1_out16, demultiplexer_1_out17, demultiplexer_1_out18, demultiplexer_1_out19,
       demultiplexer_1_out20, demultiplexer_1_out21, demultiplexer_1_out22, demultiplexer_1_out23,
       demultiplexer_1_out24, demultiplexer_1_out25, demultiplexer_1_out26, demultiplexer_1_out27,
       demultiplexer_1_out28, demultiplexer_1_out29, demultiplexer_1_out30, demultiplexer_1_out31, not_1_out,
       pull_resistor_1_node, stable_clock_1_p1, stable_clock_1_p3;
  wire [15:0] register_1_q, register_2_q;
  wire [31:0] demultiplexer_2_out31;

  assign i1 = demultiplexer_1_out0 ? demultiplexer_2_out31 : 32'bz;  // Controlled_Buffer controlled_buffer_1
  assign i3 = demultiplexer_1_out2 ? demultiplexer_2_out31 : 32'bz;  // Controlled_Buffer controlled_buffer_2
  assign i2 = demultiplexer_1_out1 ? demultiplexer_2_out31 : 32'bz;  // Controlled_Buffer controlled_buffer_3
  Demultiplexer #(.select(5), .enable("false")) demultiplexer_1 (
    .out0(demultiplexer_1_out0), .out1(demultiplexer_1_out1), .out2(demultiplexer_1_out2),
    .out3(demultiplexer_1_out3), .out4(demultiplexer_1_out4), .out5(demultiplexer_1_out5),
    .out6(demultiplexer_1_out6), .out7(demultiplexer_1_out7), .out8(demultiplexer_1_out8),
    .out9(demultiplexer_1_out9), .out10(demultiplexer_1_out10), .out11(demultiplexer_1_out11),
    .out12(demultiplexer_1_out12), .out13(demultiplexer_1_out13), .out14(demultiplexer_1_out14),
    .out15(demultiplexer_1_out15), .out16(demultiplexer_1_out16), .out17(demultiplexer_1_out17),
    .out18(demultiplexer_1_out18), .out19(demultiplexer_1_out19), .out20(demultiplexer_1_out20),
    .out21(demultiplexer_1_out21), .out22(demultiplexer_1_out22), .out23(demultiplexer_1_out23),
    .out24(demultiplexer_1_out24), .out25(demultiplexer_1_out25), .out26(demultiplexer_1_out26),
    .out27(demultiplexer_1_out27), .out28(demultiplexer_1_out28), .out29(demultiplexer_1_out29),
    .out30(demultiplexer_1_out30), .out31(demultiplexer_1_out31), .in(1'b1), .sel(cursor[9:5]));
  assign i5 = demultiplexer_1_out4 ? demultiplexer_2_out31 : 32'bz;  // Controlled_Buffer controlled_buffer_4
  assign i4 = demultiplexer_1_out3 ? demultiplexer_2_out31 : 32'bz;  // Controlled_Buffer controlled_buffer_5
  assign i6 = demultiplexer_1_out5 ? demultiplexer_2_out31 : 32'bz;  // Controlled_Buffer controlled_buffer_6
  assign i7 = demultiplexer_1_out6 ? demultiplexer_2_out31 : 32'bz;  // Controlled_Buffer controlled_buffer_7
  assign i8 = demultiplexer_1_out7 ? demultiplexer_2_out31 : 32'bz;  // Controlled_Buffer controlled_buffer_8
  assign i9 = demultiplexer_1_out8 ? demultiplexer_2_out31 : 32'bz;  // Controlled_Buffer controlled_buffer_9
  assign i11 = demultiplexer_1_out10 ? demultiplexer_2_out31 : 32'bz;  // Controlled_Buffer controlled_buffer_10
  assign i10 = demultiplexer_1_out9 ? demultiplexer_2_out31 : 32'bz;  // Controlled_Buffer controlled_buffer_11
  assign i13 = demultiplexer_1_out12 ? demultiplexer_2_out31 : 32'bz;  // Controlled_Buffer controlled_buffer_12
  assign i12 = demultiplexer_1_out11 ? demultiplexer_2_out31 : 32'bz;  // Controlled_Buffer controlled_buffer_13
  assign i15 = demultiplexer_1_out14 ? demultiplexer_2_out31 : 32'bz;  // Controlled_Buffer controlled_buffer_14
  assign i14 = demultiplexer_1_out13 ? demultiplexer_2_out31 : 32'bz;  // Controlled_Buffer controlled_buffer_15
  assign i17 = demultiplexer_1_out16 ? demultiplexer_2_out31 : 32'bz;  // Controlled_Buffer controlled_buffer_16
  assign i16 = demultiplexer_1_out15 ? demultiplexer_2_out31 : 32'bz;  // Controlled_Buffer controlled_buffer_17
  assign i18 = demultiplexer_1_out17 ? demultiplexer_2_out31 : 32'bz;  // Controlled_Buffer controlled_buffer_18
  assign i19 = demultiplexer_1_out18 ? demultiplexer_2_out31 : 32'bz;  // Controlled_Buffer controlled_buffer_19
  assign i20 = demultiplexer_1_out19 ? demultiplexer_2_out31 : 32'bz;  // Controlled_Buffer controlled_buffer_20
  assign i21 = demultiplexer_1_out20 ? demultiplexer_2_out31 : 32'bz;  // Controlled_Buffer controlled_buffer_21
  assign i23 = demultiplexer_1_out22 ? demultiplexer_2_out31 : 32'bz;  // Controlled_Buffer controlled_buffer_22
  assign i22 = demultiplexer_1_out21 ? demultiplexer_2_out31 : 32'bz;  // Controlled_Buffer controlled_buffer_23
  assign i25 = demultiplexer_1_out24 ? demultiplexer_2_out31 : 32'bz;  // Controlled_Buffer controlled_buffer_24
  assign i24 = demultiplexer_1_out23 ? demultiplexer_2_out31 : 32'bz;  // Controlled_Buffer controlled_buffer_25
  Register #(.width(16)) register_1 (.D(cursor), .Q(register_1_q), .clk(clock));  // open: en, clr
  Register #(.width(16), .trigger("falling")) register_2 (.D(cursor), .Q(register_2_q), .clk(clock));  // open: en, clr
  assign i27 = demultiplexer_1_out26 ? demultiplexer_2_out31 : 32'bz;  // Controlled_Buffer controlled_buffer_26
  assign i26 = demultiplexer_1_out25 ? demultiplexer_2_out31 : 32'bz;  // Controlled_Buffer controlled_buffer_27
  // stable_clock stable_clock_1: pin names not known; wires that end beside it: stable_clock_1_p1, clock, stable_clock_1_p3
  Comparator #(.width(16)) comparator_1 (.a(register_1_q), .b(register_2_q), .eq(stable_clock_1_p1));  // open: gt, lt
  assign i29 = demultiplexer_1_out28 ? demultiplexer_2_out31 : 32'bz;  // Controlled_Buffer controlled_buffer_28
  assign i28 = demultiplexer_1_out27 ? demultiplexer_2_out31 : 32'bz;  // Controlled_Buffer controlled_buffer_29
  not not_1 (not_1_out, stable_clock_1_p3);
  assign i30 = demultiplexer_1_out29 ? demultiplexer_2_out31 : 32'bz;  // Controlled_Buffer controlled_buffer_30
  assign i31 = demultiplexer_1_out30 ? demultiplexer_2_out31 : 32'bz;  // Controlled_Buffer controlled_buffer_31
  and and_1 (and_1_out, ~cursor[15], not_1_out);  // AND_Gate
  assign i32 = demultiplexer_1_out31 ? demultiplexer_2_out31 : 32'bz;  // Controlled_Buffer controlled_buffer_32
  Demultiplexer #(.select(5), .tristate("true")) demultiplexer_2 (
    .out0(demultiplexer_2_out31[31]), .out1(demultiplexer_2_out31[30]), .out2(demultiplexer_2_out31[29]),
    .out3(demultiplexer_2_out31[28]), .out4(demultiplexer_2_out31[27]), .out5(demultiplexer_2_out31[26]),
    .out6(demultiplexer_2_out31[25]), .out7(demultiplexer_2_out31[24]), .out8(demultiplexer_2_out31[23]),
    .out9(demultiplexer_2_out31[22]), .out10(demultiplexer_2_out31[21]), .out11(demultiplexer_2_out31[20]),
    .out12(demultiplexer_2_out31[19]), .out13(demultiplexer_2_out31[18]), .out14(demultiplexer_2_out31[17]),
    .out15(demultiplexer_2_out31[16]), .out16(demultiplexer_2_out31[15]), .out17(demultiplexer_2_out31[14]),
    .out18(demultiplexer_2_out31[13]), .out19(demultiplexer_2_out31[12]), .out20(demultiplexer_2_out31[11]),
    .out21(demultiplexer_2_out31[10]), .out22(demultiplexer_2_out31[9]), .out23(demultiplexer_2_out31[8]),
    .out24(demultiplexer_2_out31[7]), .out25(demultiplexer_2_out31[6]), .out26(demultiplexer_2_out31[5]),
    .out27(demultiplexer_2_out31[4]), .out28(demultiplexer_2_out31[3]), .out29(demultiplexer_2_out31[2]),
    .out30(demultiplexer_2_out31[1]), .out31(demultiplexer_2_out31[0]), .in(pull_resistor_1_node),
    .sel(cursor[4:0]), .en(and_1_out));
  Pull_Resistor #(.pull("X")) pull_resistor_1 (.node(pull_resistor_1_node));

  assign o1 = i1;
  assign o2 = i2;
  assign o3 = i3;
  assign o4 = i4;
  assign o5 = i5;
  assign o6 = i6;
  assign o7 = i7;
  assign o8 = i8;
  assign o9 = i9;
  assign o10 = i10;
  assign o11 = i11;
  assign o12 = i12;
  assign o13 = i13;
  assign o14 = i14;
  assign o15 = i15;
  assign o16 = i16;
  assign o17 = i17;
  assign o18 = i18;
  assign o19 = i19;
  assign o20 = i20;
  assign o21 = i21;
  assign o22 = i22;
  assign o23 = i23;
  assign o24 = i24;
  assign o25 = i25;
  assign o26 = i26;
  assign o27 = i27;
  assign o28 = i28;
  assign o29 = i29;
  assign o30 = i30;
  assign o31 = i31;
  assign o32 = i32;
endmodule
